# Fritzing sketch isp_programmer (saved by Fritzing 1.0.1rc)
circuit board: 7.03285cm x 5.43817cm

parts:
  J1 = female pin header, 4 pins [form="♀ (female)"]
  J2 = female pin header, 4 pins [form="♀ (female)"]
  Shield = Arduino Proto Shield
  J3 = female pin header, 4 pins [form="♀ (female)"]
  J4 = female pin header, 4 pins [form="♀ (female)"]
  R2 = Resistor [tolerance=±5% power=0.25 resistance=100 package=THT]
  R3 = Resistor [tolerance=±5% power=0.25 resistance=100 package=THT]
  LED2 = LED - 3mm [color="Red (633nm)" current=0.030 package="3 mm [THT]"]
  LED1 = LED - 3mm [color="Green (555nm)" current=0.030 package="3 mm [THT]"]
  J6 = male pin header, 4 pins [form="♂ (male)"]
  J7 = male pin header, 4 pins [form="♂ (male)"]
  J8 = male pin header, 4 pins [form="♂ (male)"]
  J9 = male pin header, 4 pins [form="♂ (male)"]
  J10 = male pin header, 3 pins [form="♂ (male)"]
  J11 = male pin header, 3 pins [form="♂ (male)"]
  R1 = Resistor [tolerance=±5% power=0.25 resistance=100 package=THT]
  S2 = SWITCH-DPDT [package=es]
  S1 = Custom switch [package="thru hole"]
  LED3 = LED - 3mm [color="Yellow (595nm)" current=0.030 package="3 mm [THT]"]

nets:
  N1: J1.pin1, Shield.pad_140, Shield.pad_386, Shield.Reset, J11.pin3, S1.2
  AT 2: J1.pin2, Shield.pad_72, Shield.pad_98, Shield.pad_139, J3.pin2, J6.pin2
  AT 3: J1.pin3, Shield.pad_71, Shield.pad_97, Shield.pad_138, J3.pin3, J6.pin3
  AT 4: J1.pin4, Shield.pad_70, Shield.pad_96, Shield.pad_106, Shield.pad_132, Shield.pad_137, Shield.pad_159, Shield.pad_363, Shield.GNS, J3.pin4, LED2.cathode, LED1.cathode, J6.pin4, J10.pin1, S2.2, LED3.cathode
  AT 8: J2.pin1, Shield.pad_173, Shield.pad_197, Shield.pad_213, Shield.pad_361, Shield.+5V#connector_IcspV5v, J4.pin1, J7.pin1, J10.pin3, S2.5
  N2: J2.pin2, Shield.pad_212, Shield.pad_353, Shield.SCK, J11.pin2, S1.14
  N3: J2.pin3, Shield.pad_211, Shield.pad_349, Shield.MISO, J11.pin1, S1.10
  N4: J2.pin4, Shield.pad_210, Shield.pad_390, Shield.MOSI, J10.pin2, S1.6
  N5: Shield.pad_19, Shield.pad_45, J9.pin4
  N6: Shield.pad_20, Shield.pad_46, J9.pin3
  N7: Shield.pad_21, Shield.pad_47, J9.pin2
  N8: Shield.pad_22, Shield.pad_48, J9.pin1
  AT 1: Shield.pad_73, Shield.pad_99, Shield.pad_385, J3.pin1, J6.pin1, S1.1
  N9: Shield.pad_81, Shield.pad_107, LED1.anode, R1.Pin_1
  N10: Shield.pad_82, Shield.pad_133, R2.Pin_1, LED2.anode
  N11: Shield.pad_83, Shield.pad_160, R3.Pin_1, LED3.anode
  AT 5: Shield.pad_170, Shield.pad_194, Shield.pad_389, J4.pin4, J7.pin4, S1.5
  AT 6: Shield.pad_171, Shield.pad_195, Shield.pad_348, J4.pin3, J7.pin3, S1.9
  AT 7: Shield.pad_172, Shield.pad_196, Shield.pad_352, J4.pin2, J7.pin2, S1.13
  N12: Shield.pad_221, Shield.pad_247, J8.pin4
  N13: Shield.pad_222, Shield.pad_248, J8.pin3
  N14: Shield.pad_223, Shield.pad_249, J8.pin2
  N15: Shield.pad_224, Shield.pad_250, J8.pin1
  N16: Shield.pad_338, S2.6
  N17: Shield.pad_340, S2.3
  N18: Shield.pad_350, S1.11
  N19: Shield.pad_351, Shield.D12, S1.12
  N20: Shield.pad_354, S1.15
  N21: Shield.pad_355, Shield.D13, S1.16
  N22: Shield.pad_387, S1.3
  N23: Shield.pad_388, Shield.D10, S1.4
  N24: Shield.pad_391, S1.7
  N25: Shield.pad_392, Shield.D11, S1.8
  N26: Shield.D7, R3.Pin_0
  N27: Shield.D8, R2.Pin_0
  N28: Shield.D9, R1.Pin_0
  N29: Shield.GND, S2.1
  N30: Shield.+5V#connector_V5v, Shield.+5V#connector_V5v-b, S2.4

notes:
  AT tiny
  4  3  2  1
  5  6  7  8

custom parts:
  Arduino Proto Shield: Arduino prototyping shield by diymore.cc
  SWITCH-DPDT: DPDT Version of the COM-00597
  Custom switch: quadruple 3 positions swtch
